// Digital circuit SOP.dig as structural Verilog
module SOP (
  input  A,
  input  B,
  input  C,
  input  D,
  output Y
);

  wire not_1_out, not_2_out, not_3_out, not_4_out;

  not not_1 (not_1_out, A);
  not not_2 (not_2_out, B);
  not not_3 (not_3_out, C);
  not not_4 (not_4_out, D);
  // And and_1 is placed but not wired
  // And and_2 is placed but not wired
  // Or or_1 has open pins: In_1=open, In_2=open, out=Y

  // Notes on the sheet:
  //   A: MSB
  //   D: LSB
  //   Use A as the most-significant bit and 
  //   D as the least-significant bit.
endmodule

/* Test case:
A B C D Y
0 0 0 0 X
0 0 0 1 1
*/
